// Digital circuit 8-bit_GPR.dig as structural Verilog
module _8_bit_GPR (
  input  CLK,
  input  [1:0] CTRL,
  input  [1:0] RegisterSelection,
  input  [7:0] Input,
  output [7:0] Output
);

  wire and_1_out, and_2_out, and_3_out, and_4_out, decoder_1_out_0, decoder_1_out_1, decoder_1_out_2,
       decoder_1_out_3;
  wire [7:0] R_0_p4, R_1_p4, R_2_p4, R_3_p4;

  Decoder #(.Selector_Bits(2)) decoder_1 (
    .sel(RegisterSelection), .out_0(decoder_1_out_0), .out_1(decoder_1_out_1), .out_2(decoder_1_out_2),
    .out_3(decoder_1_out_3));
  and and_1 (and_1_out, decoder_1_out_0, CLK);
  and and_2 (and_2_out, decoder_1_out_1, CLK);
  and and_3 (and_3_out, decoder_1_out_2, CLK);
  and and_4 (and_4_out, decoder_1_out_3, CLK);
  // _8_bit_Register R_0: pin names not known; wires that end beside it: and_1_out, Input, CTRL, R_0_p4
  // _8_bit_Register R_1: pin names not known; wires that end beside it: and_2_out, Input, CTRL, R_1_p4
  // _8_bit_Register R_2: pin names not known; wires that end beside it: and_3_out, Input, CTRL, R_2_p4
  // _8_bit_Register R_3: pin names not known; wires that end beside it: and_4_out, Input, CTRL, R_3_p4
  Multiplexer #(.Bits(8), .Selector_Bits(2)) multiplexer_1 (
    .sel(RegisterSelection), .in_0(R_0_p4), .in_1(R_1_p4), .in_2(R_2_p4), .in_3(R_3_p4), .out(Output));

  // Notes on the sheet:
  //   00 - Load
  //   01 - Store
  //   10 - Clear
  //   11 - Set FF
endmodule
