// Digital circuit 8-bit_IR.dig as structural Verilog
module _8_bit_IR (
  input  [1:0] CTRL_Input,
  input  [7:0] SRAM_Data,
  input  [7:0] Input,
  input  CLK,
  input  MUX_Select,
  output [7:0] Output
);

  wire [7:0] multiplexer_1_out;

  Multiplexer #(.Bits(8)) multiplexer_1 (.sel(MUX_Select), .in_0(SRAM_Data), .in_1(Input), .out(multiplexer_1_out));
  // _8_bit_Register _8_bit_register_1: pin names not known; wires that end beside it: CLK, multiplexer_1_out, CTRL_Input, Output

  // Notes on the sheet:
  //   CTRL_Input: 00 - Load
  //   01 - INC
  //   10 - Reset
  //   11 - Set
  //   00 - Load
endmodule
