// Digital circuit SRAM.dig as structural Verilog
module SRAM (
  input  [1:0] CTRL_Input,
  input  [7:0] PC_Output,
  input  [3:0] MAN_Address,
  input  A_Selector,
  input  clk,
  input  [7:0] Data_In,
  output [7:0] Data_Output
);

  wire and_1_out, and_2_out, and_3_out, and_4_out, not_1_out, not_2_out, or_1_out;
  wire [3:0] multiplexer_1_out;
  wire [7:0] multiplexer_2_out;

  not not_1 (not_1_out, CTRL_Input[0]);
  not not_2 (not_2_out, CTRL_Input[1]);
  and and_1 (and_1_out, not_1_out, not_2_out);
  and and_2 (and_2_out, not_2_out, CTRL_Input[0]);
  and and_3 (and_3_out, not_1_out, CTRL_Input[1]);
  and and_4 (and_4_out, CTRL_Input[0], CTRL_Input[1]);
  or or_1 (or_1_out, and_2_out, and_3_out, and_4_out);
  Multiplexer #(.Bits(4)) multiplexer_1 (
    .sel(A_Selector), .in_0(PC_Output[7:4]), .in_1(MAN_Address), .out(multiplexer_1_out));
  Multiplexer #(.Bits(8), .Selector_Bits(2)) multiplexer_2 (
    .sel(CTRL_Input), .in_0(Data_In), .in_1(Data_In), .in_2({8{1'b0}}), .in_3(8'h1), .out(multiplexer_2_out));
  RAMDualPort #(.AddrBits(4), .Bits(8)) ramdualport_1 (
    .A(multiplexer_1_out), .Din(multiplexer_2_out), .str(or_1_out), .C(clk), .ld(and_1_out), .D(Data_Output));

  // Notes on the sheet:
  //   CTRL_Input: 00 - Load
  //   01 - INC
  //   10 - Reset
  //   11 - Set
  //   00 - Load
  //   01 - Store
  //   10 - Clear
  //   11 - Set FF
endmodule
